# Fritzing sketch LcdPanel (saved by Fritzing 0.9.2b)
circuit board: 8.46667cm x 5.64444cm
breadboards: 1

parts:
  LCD1 = LCD screen
  R1 = Trimmer Potentiometer [maximum_resistance=10kΩ package=THT]
  Part1 = Arduino Uno (Rev3)
  IR1 = TSOP312.., 314.. [package=THT]
  C1 = Ceramic Capacitor [capacitance=100nF package="100 mil [THT, multilayer]"]
  Часть2 = Real Time Clock Module - DS1307 RTC Breakout Board
  J1 = Piezo Speaker

nets:
  GND: LCD1.VSS, LCD1.R/W, LCD1.DB0, LCD1.DB1, LCD1.DB2, LCD1.DB3, LCD1.LED-, R1.leg1, Part1.GND, IR1.Vs, C1.0, Часть2.GND, J1.pin1
  5V: LCD1.VDD, R1.leg2, Part1.5V, IR1.Data, C1.1, Часть2.5V
  N1: LCD1.V0, R1.wiper
  N2: LCD1.RS, Part1.D10_PWM/SS
  N3: LCD1.E, Part1.D12/MISO
  N4: LCD1.DB4, Part1.D6_PWM
  N5: LCD1.DB5, Part1.D7
  N6: LCD1.DB6, Part1.D8
  N7: LCD1.DB7, Part1.D9_PWM
  N8: LCD1.LED+, Part1.D11_PWM/MOSI
  N9: Part1.A5/SCL, J1.pin2
  N10: Part1.D2, IR1.GND
  N11: Part1.D3_PWM, Часть2.SDA
  N12: Part1.D4, Часть2.SCL
  N13: Part1.D5_PWM, Часть2.SQW

notes:
  Подключение LCD
  дисплея

// code stored in the sketch: LcdPanel.ino
/*
 */
#include <IrControl.h>
#include <LiquidCrystal.h>

// указываем пин для ИК датчика 
IrControl control(2);
// initialize the library with the numbers of the interface pins
LiquidCrystal lcd(12, 10, 6, 7, 8, 9);

void setup() {
  Serial.begin(9600);
  // set up the LCD's number of columns and rows:
  lcd.begin(16, 2);
  lcd.clear();
  lcd.print("Start");
  control.start();
}

void loop() {
/*  int thisChar = 0;
  for (int row = 0; row < 16; row++) {
    lcd.setCursor(0, row % 2);
    for (int col = 0; col < 16; col++) {
      lcd.write(thisChar++);
    }
    if (row % 2 == 1) {*/
//  Serial.print(".");

  if (control.hasCode()) {
    long code = control.getCode();
    char key = control.toKey(code);
    Serial.print("IR key = ");
    if (key == 0) {
      Serial.print("NOTHIN");
    } else {
      Serial.print(key);
    }
    Serial.print("; code = ");
    Serial.println(control.code, HEX);
    lcd.setCursor(0, 0);
    lcd.print("IR key = ");
    if (key == 0) {
      lcd.print("NOTHIN");
    } else {
      lcd.print(key);
      lcd.print("       ");
    }
    lcd.setCursor(0, 1);
    lcd.print("code = ");
    lcd.print(control.code, HEX);
    lcd.print("       ");
//    delay(1000);
  }
  delay(100);
/*    }
  }*/

/*
    switch (key) {
      case 's':
      break;
      case 'r':
      break;
      case 'f':
      break;
      case 'l':
      break;
      case 'b':
        beforeCommandSet();
        showCom++;
        if (showCom > 5) {
          showCom = 0;
        }
        afterCommandSet();
      break;
      case 't':
        beforeCommandSet();
        showCom--;
        if (showCom < 0) {
          showCom = 5;
        }
        afterCommandSet();
      break;
    }
*/
}
