# Fritzing sketch TimePanel (saved by Fritzing 0.9.2b)
circuit board: 8.46667cm x 5.64444cm
breadboards: 1

parts:
  Часть1 = Arduino Uno (Rev3)
  U2 = 74HC595 [package="DIP16 [THT]"]
  R1 = Resistor [tolerance=±5% resistance=220 package=THT]
  R2 = Resistor [tolerance=±5% resistance=220 package=THT]
  R3 = Resistor [tolerance=±5% resistance=220 package=THT]
  R4 = Resistor [tolerance=±5% resistance=220 package=THT]
  LED1 = 7-SEGMENT-4DIGIT-YOUNGSUN [package=7-segment-4digit-youngsun]
  R5 = Trimmer Potentiometer [maximum_resistance=10kΩ package=THT]
  IR1 = TSOP312.., 314.. [package=THT]
  C1 = Ceramic Capacitor [capacitance=100nF package="100 mil [THT, multilayer]"]
  J1 = Basic Servo

nets:
  N1: Часть1.A0, R5.wiper
  N2: Часть1.D8, U2.ST_CP
  N3: Часть1.D9_PWM, R2.Pin_1
  N4: Часть1.D10_PWM/SS, R1.Pin_0
  N5: Часть1.D11_PWM/MOSI, U2.DS
  N6: Часть1.D12/MISO, U2.SH_CP
  N7: Часть1.D2, IR1.GND
  N8: Часть1.D4, R4.Pin_1
  N9: Часть1.D5_PWM, J1.pulse
  N10: Часть1.D7, R3.Pin_1
  VCC: Часть1.5V, U2.MR, U2.VCC, R5.leg1, J1.vcc
  GND: Часть1.GND, U2.GND, U2.OE, R5.leg2, IR1.Vs, IR1.Data, C1.0, C1.1, J1.gnd
  N11: U2.Q1, LED1.DIG2
  N12: U2.Q2, LED1.A
  N13: U2.Q3, LED1.DIG3
  N14: U2.Q4, LED1.D
  N15: U2.Q5, LED1.APOS-A
  N16: U2.Q6, LED1.E
  N17: U2.Q7, LED1.COL-A
  N18: U2.Q0, LED1.C
  N19: R1.Pin_1, LED1.G
  N20: R2.Pin_0, LED1.COL-C
  N21: R3.Pin_0, LED1.F
  N22: R4.Pin_0, LED1.DP

// code stored in the sketch: IR_Test.ino
/*
#define READ_BUF_SIZE 400
short readBuf[READ_BUF_SIZE];
*/
const int irPin = 2;

#define IR_INTERRUPT_BUF_SIZE 66

#define IR_TEST_MINIMAL_TIME 200
#define IR_TEST_MAXIMAL_TIME 20000
#define IR_TEST_MINIMAL_COUNT 14
#define IR_TEST_MAXIMAL_COUNT 1300
#define IR_TEST_BOUND_COUNT 80

//volatile int IRTestCount = -1;
volatile long IRTestStartTime = 0;
//volatile long IRTestTimes[IR_INTERRUPT_BUF_SIZE];
//volatile byte IRTestValues[IR_INTERRUPT_BUF_SIZE];

void initIRTest() {
  pinMode(irPin, INPUT);
  startIRTest();
}
void startIRTest() {
  attachInterrupt(digitalPinToInterrupt(irPin), IRTestInterrupt, CHANGE);
}
void stopIRTest() {
  detachInterrupt(digitalPinToInterrupt(irPin));
}

void IRTestInterrupt() {
  long time = micros() - IRTestStartTime;
  IRTestStartTime += time;
  timePanel++;
  if (time < IR_TEST_MINIMAL_TIME || time > IR_TEST_MAXIMAL_TIME) {
    return;
  }
  byte value = digitalRead(irPin);
  if (value == HIGH && time > 3000 && time <= IR_TEST_MAXIMAL_TIME) {
    noInterrupts();
    int count = IR_TEST_MAXIMAL_COUNT;
    if (
      //(count = IRTestWhite(LOW)) < IR_TEST_MAXIMAL_COUNT &&
      (count = IRTestWhite(HIGH)) < IR_TEST_MAXIMAL_COUNT
    ) {
      IRTestDecode();
    }
    interrupts();
  }
}

boolean IRTestDecode() {
  long value = 0;
  for (int i = 0; i < 32; i++) {
    int count = IRTestWhite(LOW);
    if (count < IR_TEST_MINIMAL_COUNT || count >= IR_TEST_BOUND_COUNT) {
      /* IRTestCount = i;
      IRTestValue = count;
      IRTestHasValue = true; */
      return false;
    }
    count = IRTestWhite(HIGH);
    if (count < IR_TEST_MINIMAL_COUNT || count >= IR_TEST_MAXIMAL_COUNT) {
      /*IRTestCount = i + 1000;
      IRTestValue = count;
      IRTestHasValue = true;*/
      return false;
    }
    value <<= 1;
    value |= (count > IR_TEST_BOUND_COUNT) ? 1 : 0;
  }
  IRTestValue = value;
  IRTestHasValue = true;
  return true;
}

/** пропускаем пока и считаем время */
int IRTestWhite(byte val) {
  int count = 0;
  while (digitalRead(irPin) == val && count < IR_TEST_MAXIMAL_COUNT) {
    delayMicroseconds(10);
    count ++;
  }
  return count;
}

/*
void IRTestCheck() {
  Serial.print("----- timePanel = ");
  Serial.print(timePanel);
  Serial.println("; -----");
  for (int i = 0; i < IR_INTERRUPT_BUF_SIZE; i++) {
    Serial.print(i);
    Serial.print(": time = ");
    Serial.print(IRTestTimes[i], DEC);
    Serial.print("; value = ");
    Serial.print(IRTestValues[i], DEC);
    Serial.println("; | ");
  }
  Serial.print("----- timePanel = ");
  Serial.print(timePanel);
  Serial.println("; -----");
  timePanel=0;
}
void IRTestEvent() {
  long time = millis();
  for (int i = 0; i < READ_BUF_SIZE; i++) {
    short val = 0;
    for (int k = 0; k < 16; k++) {
      val = val << 1;
      val |= digitalRead(irPin);
      delayMicroseconds(10);
    }
    readBuf[i] = val;
  }
  time = millis() - time;

  char outChars[30];
  Serial.print("------- ");
  Serial.print(time);
  Serial.println(" ------------------------");
  for (int i = 0; i < READ_BUF_SIZE; i++) {
    short val = readBuf[i];
    //Serial.println(readBuf[i] & 0xffff, BIN);    
    for (int k = 0; k < 16; k++) {
      Serial.print((val & 0x8000) ? '#' : '_');
      val = val << 1;
    }
    if (i % 8 == 0) {
      Serial.println(" |");
    }
  }
  Serial.print("------- ");
  Serial.print(time);
  Serial.println(" ------------------------");
}
*/
/*
void IRTestRead() {
  char outChars[30];
  long time = millis();
  for (int i = 0; i < READ_BUF_SIZE; i++) {
    readBuf[i] = digitalRead(irPin);
    delayMicroseconds(100);
  }
  time = millis() - time;

  Serial.print("------- ");
  Serial.print(time);
  Serial.println(" ------------------------");
  for (int i = 0; i < READ_BUF_SIZE; i++) {
    Serial.print(readBuf[i] / 204.8);
    char outChars[30];
    int j = 0;
    for (; j < readBuf[i] / 51.2; j++) {
      outChars[j] = '.';
    }
    outChars[j++] = '#';
    outChars[j++] = 0;
    Serial.println(outChars);
  }
  Serial.print("------- ");
  Serial.print(time);
  Serial.println(" ------------------------");
}
*/

// code stored in the sketch: ShowPanel.ino
#include <MsTimer2.h>

#define DIGIT_ON  HIGH
#define DIGIT_OFF LOW

#define MINUS_MASK 8

//Пин подключен к ST_CP входу 74HC595
const int latchPin = 8;
//Пин подключен к SH_CP входу 74HC595
const int clockPin = 12;
//Пин подключен к DS входу 74HC595
const int dataPin = 11;

const int digit[4] = {10,9,7,4};

const byte segmentMap[16] = {
//   -0-        -1-        -2-        -3-        -4-        -5-        -6-        -7-    
  B01110111, B01100000, B00111110, B01111100, B01101001, B01011101, B01011111, B01100100,
//   -8-        -9-        -A-        -B-        -C-        -D-        -E-        -F-
  B01111111, B01111101, B01101111, B01011011, B00010111, B01111010, B00011111, B00001111
};

void initPanel() {
  //устанавливаем режим OUTPUT
  pinMode(latchPin, OUTPUT);
  pinMode(clockPin, OUTPUT);
  pinMode(dataPin, OUTPUT);

  for (int i = 0; i < 4; i++) { 
    pinMode(digit[i], OUTPUT);
  }
  MsTimer2::set(5, showPanel);
  MsTimer2::start();
}

/** показываем очередной сегмент. */
void showPanel2() {
  static int chars = 0;
  resetAllDigit();
  setChar('a' + chars, true);
  digitalWrite(digit[chars], DIGIT_ON);
  chars++;
  if (!(chars < 4)) {
    chars = 0;
  }
}

/** показываем очередной сегмент. */
void showPanel() {
  static int place = 0;
  static int chars = 0;
  static String panelValueLocal = panelValue;
  resetAllDigit();
  if (chars < panelValueLocal.length()) {
    char chr = panelValueLocal[chars];
    if (chars + 1 < panelValueLocal.length() && panelValueLocal[chars + 1] == '.') {
      setChar(chr, true);
      chars++;
    } else {
      setChar(chr, false);
    }
    digitalWrite(digit[place], DIGIT_ON);
  }
  place++;
  chars++;
  if (!(place < 4 && chars < panelValueLocal.length())) {
    place = 0;
    chars = 0;
    panelValueLocal = panelValue;
  }
}

/** Сбрасываем все цифры. */
void resetAllDigit() {
  for (int digInd = 0; digInd < 4; digInd++) {
    int dig = digit[digInd];
    digitalWrite(dig, DIGIT_OFF);
  }
}

/** Находим маску по номеру знака(цифры) и выводим маску в сегменты */ 
void setChar(char chr, boolean isPnt) {
  int bits;
  if (chr == '-') {
    bits = MINUS_MASK;
  } else if (chr >= '0' && chr <= '9') {
    bits = segmentMap[chr - '0'];
  } else if (chr >= 'a' && chr <= 'f') {
    bits = segmentMap[chr - 'a' + 10];
  } else if (chr >= 'A' && chr <= 'F') {
    bits = segmentMap[chr - 'A' + 10];
  } else {
    bits = 127;
  }
  if (isPnt) {
    bits |= 128;
  }
  setNumBit(bits);
}

/** Выводит маску символа в сегменты */
void setNumBit(uint8_t mask) {
  // устанавливаем синхронизацию "защелки" на LOW
  digitalWrite(latchPin, LOW);
  // передаем последовательно на dataPin
  shiftOut(dataPin, clockPin, MSBFIRST, mask ^ 0xFF);
  //"защелкиваем" регистр, тем самым устанавливая значения на выходах
  digitalWrite(latchPin, HIGH);
}

// code stored in the sketch: TimePanel.ino
#include <Servo.h>

// create servo object to control a servo
Servo myservo;

//Пин подключен к резистору
const int resistorPin = A0;
//Пин подключен к резистору
const int motorPin = 5;

/**  */
String panelValue = "";
volatile long timePanel = 0;
//volatile int IRTestCount = -1;
volatile long IRTestValue = 0;
volatile boolean IRTestHasValue = false;
int showCom = 0;

void setup() {
  Serial.begin(9600);
  myservo.attach(motorPin);
  initPanel();
  //initIRControl();
  initIRTest();
}

void loop() {
  switch (showCom) {
    case 0:
      setTimeToPanel();
      break;
    case 1: {
        int resistorValue = analogRead(resistorPin);
        myservo.write(map(resistorValue, 0, 1023, 0, 180));
        panelValue = String((resistorValue * 180.0) / 1023, 2);
      }
      break;
    case 2:
      setIRTestToPanel();
      break;
    case 3:
      panelValue = "-03-";
      break;
    case 4:
      panelValue = "-04-";
      break;
    default:
      panelValue = "defa";
      break;
  }

  if (IRTestHasValue) {
    IRTestHasValue = false;
    //setIRTestToPanel();

    /*
        Serial.print("bit = ");
        Serial.print(IRTestCount);
    */
    Serial.print("key = ");
    Serial.println(IRTestValue, HEX);

    if (IRTestValue == 0xFFA857) {
      shimmiDance();
    } else if (IRTestValue == 0xFFE01F) {
      myservo.write(180);
      delay(1000);
    } else if (IRTestValue == 0xFF02FD) {
      myservo.write(90);
      delay(1000);
    } else if (IRTestValue == 0xFF906F) {
      myservo.write(0);
      delay(1000);
    } else if (IRTestValue == 0xFFC23D) {
      showCom++;
      if (showCom > 3) {
        showCom = 0;
      }
    }
  }
  delay(100);
}

void setTimeToPanel() {
  static int count = 0;
  panelValue = timeToString(count == 0);
  if (count >= 600) {
    //showDoubleOut();
    count = 0;
  } else {
    count++;
  }
}

void setIRTestToPanel() {
  String value = String(IRTestValue, HEX);
  int len = value.length();
  if (len > 4) {
    panelValue = value.substring(len - 4, len);
  } else {
    panelValue = value;
  }
}

void serialEvent() {
  char buf[10];
  int cnt = Serial.readBytes(buf, 10) - 1;
  if (cnt >= 0 && cnt < 10) {
    buf[cnt] = 0;
  }
  panelValue = String(buf);
  Serial.println("\"" + panelValue + "\"");
  //IRTestCheck();
  //IRTestRead();
  //IRTestEvent();
  boolean isDigits = true;
  for (int i = 0; i < cnt; i++) {
    if (!isDigit(buf[i])) {
      isDigits = false;
    }
  }
  if (isDigits) {
    int degre = panelValue.toInt();
    if (degre >= 0 && degre <= 180) {
      myservo.write(degre);
    }
  } else {
    shimmiDance();
  }

  delay(2000);
}

void shimmiDance() {
  int i = myservo.read();
  for (int j = 0; j < 3; j++) {
    for (i++; i <= 180; i++) {
      panelValue = String(i, DEC);
      myservo.write(i);
      //Serial.println(i);
      if (i % 90 == 0) {
        delay(1000);
      } else if (i % 30 == 0) {
        delay(300);
      } else {
        delay(30);
      }
    }
    for (i--; i >= 0; i--) {
      panelValue = String(i, DEC);
      myservo.write(i);
      //Serial.println(i);
      if (i % 90 == 0) {
        delay(1000);
      } else if (i % 30 == 0) {
        delay(300);
      } else {
        delay(30);
      }
    }
  }
}

String timeToString(boolean isSerialPrint) {
  unsigned long time = millis();
  boolean halfsec = (time % 1000) < 500;
  time /= 1000;
  int sec = time % 60;
  time /= 60;
  int min = time % 60;
  time /= 60;
  int hour = time;
  if (isSerialPrint) {
    Serial.print("hour = ");
    Serial.print(hour);
    Serial.print("; min = ");
    Serial.print(min);
    Serial.print("; sec = ");
    Serial.print(sec);
    Serial.println(";");
  }
  if (hour > 0) {
    return toTwo(hour) + (halfsec ? "." : "") + toTwo(min);// + ((sec & 1) ? "." : "");
  } else {
    return toTwo(min) + (halfsec ? "." : "") + toTwo(sec);// + ((sec & 1) ? "." : "");
  }
}

String toTwo(int val) {
  String str = "00";
  str = str + val;
  return str.substring(str.length() - 2);
}

void showDoubleOut() {
  for (double val = -11.0; val < 11.0; val += .01) {
    panelValue = String(val, 2);
    delay(100);
  }
  panelValue = "B.0.b.a.";
  delay(10000);
}
