# Fritzing sketch breadboard (saved by Fritzing 0.9.2b)
circuit board: 16.9333cm x 5.64444cm
breadboards: 1

parts:
  XTAL1 = CRYSTAL - kHz [frequency="32 kHz"]
  IC2 = DS1302 [package="DIP8 [THT]"]
  part = DS1302 [package="DIP8 [THT]"]  # not connected
  Part1 = Arduino Uno (Rev3)

nets:
  N1: XTAL1.pin_0, IC2.X2_-_Crystal
  N2: XTAL1.pin_1, IC2.X1_-_Crystal
  N3: IC2.+V, Part1.5V
  N4: IC2.0V, Part1.GND
  N5: IC2.CE_-_Chip_Enable, Part1.D5_PWM
  N6: IC2.I/O_-_SPI_Data_In/Out, Part1.D6_PWM
  N7: IC2.SCLK_-_SPI_Clock, Part1.D7
